// Digital circuit lab1-1.2-b.dig as structural Verilog
module lab1_1_2_b (
  input  W,
  input  X,
  input  Z,
  input  Y,
  output F
);

  wire and_1_out, and_2_out, and_3_out, and_4_out, and_5_out, not_1_out, not_2_out, not_3_out, not_4_out,
       or_1_out;

  not not_1 (not_1_out, X);
  not not_2 (not_2_out, Y);
  not not_3 (not_3_out, X);
  not not_4 (not_4_out, W);
  and and_1 (and_1_out, W, X, Y, not_1_out);
  and and_2 (and_2_out, W, X, not_2_out, X);
  and and_3 (and_3_out, W, not_3_out, Y, X);
  and and_4 (and_4_out, not_4_out, X, Y, X);
  and and_5 (and_5_out, W, X, Y, X);
  or or_1 (or_1_out, and_1_out, and_2_out, and_3_out, and_4_out);
  and and_6 (F, and_5_out, or_1_out);

  assign Z = X;
endmodule
